// Logisim project Final data path.circ as structural Verilog: 1 circuit, main circuit main
module main (
  input  Accept_full_word_display,
  input  [6:0] in_2,
  input  [6:0] in_3,
  input  [6:0] in_4,
  input  [6:0] in_5,
  input  [6:0] in_6,
  input  [6:0] in_7,
  input  [6:0] in_8,
  input  [6:0] in_9,
  input  Reset1,
  input  Ccontrol_Letter,
  input  Clk,
  input  RESET_2,
  input  [6:0] Letter_input,
  input  FAUND,
  input  \Load_İnpput ,
  input  \MİSS ,
  output ACCEPT,
  output [2:0] Rom_A,
  output [2:0] \LOCATİON ,
  output [3:0] Length,
  output enable_tty,
  output There_is_match,
  output [3:0] Faund_table,
  output No_Match,
  output faund_2,
  output tty_clear,
  output \İnput__İnput_Kontrol ,
  output \İnput_0 ,
  output \mİSS_2 ,
  output CAUNT_LETTER,
  output [3:0] \MİSS_TABLE 
);

  wire and_1_out, and_2_out, comparator_1_eq, comparator_2_eq, comparator_3_gt, comparator_5_eq,
       comparator_8_gt, comparator_9_lt, comparator_10_eq, d_ff_1_q;
  wire [2:0] counter_1_q, counter_2_q, counter_5_q;
  wire [3:0] counter_4_q;
  wire [6:0] multiplexer_1_out, multiplexer_2_out, register_1_q;
  wire [7:0] counter_6_q;

  Counter #(.width(3), .max('h7), .ongoal("stay")) counter_1 (
    .count(\Load_İnpput ), .Q(counter_1_q), .clk(Clk), .clr(RESET_2));  // open: load, D, carry
  Register #(.width(7), .trigger("high")) register_1 (
    .D(Letter_input), .en(\Load_İnpput ), .Q(register_1_q), .clk(Clk));  // open: clr
  Multiplexer #(.select(3), .width(7)) multiplexer_1 (
    .in0(in_2), .in1(in_3), .in2(in_4), .in3(in_5), .in4(in_6), .in5(in_7), .in6(in_8), .in7(in_9),
    .out(multiplexer_1_out), .sel(counter_2_q));  // open: en
  Counter #(.width(3), .max('h7), .ongoal("stay")) counter_2 (
    .Q(counter_2_q), .clk(Clk), .clr(Reset1));  // open: load, D, count, carry
  Multiplexer #(.select(3), .width(7)) multiplexer_2 (
    .in0(in_2), .in1(in_3), .in2(in_4), .in3(in_5), .in4(in_6), .in5(in_7), .in6(in_8), .in7(in_9),
    .out(multiplexer_2_out), .sel(counter_1_q));  // open: en
  Comparator #(.width(7)) comparator_1 (.a(multiplexer_2_out), .b(register_1_q), .eq(comparator_1_eq));  // open: gt, lt
  Comparator #(.width(3)) comparator_2 (.a(counter_1_q), .b(3'b111), .eq(comparator_2_eq));  // open: gt, lt
  Comparator #(.width(7), .mode("unsigned")) comparator_3 (
    .a(multiplexer_1_out), .b({7{1'b0}}), .gt(comparator_3_gt));  // open: eq, lt
  D_Flip_Flop d_ff_1 (.clk(Clk), .D(comparator_1_eq), .Q(d_ff_1_q));  // open: Qn, preset, en, reset
  Comparator #(.width(7)) comparator_4 (
    .a(register_1_q), .b(Letter_input), .eq(\İnput__İnput_Kontrol ));  // open: gt, lt
  and and_1 (and_1_out, comparator_3_gt, Clk);
  D_Flip_Flop d_ff_2 (.clk(Clk), .D(comparator_2_eq), .Q(CAUNT_LETTER));  // open: Qn, preset, en, reset
  Counter #(.width(4), .max('h8), .ongoal("stay")) counter_3 (
    .Q(Length), .clk(and_1_out), .clr(Reset1));  // open: load, D, count, carry
  Counter #(.width(4), .max('h8)) counter_4 (
    .Q(counter_4_q), .clk(d_ff_1_q), .clr(RESET_2));  // open: load, D, count, carry
  Hex_Digit_Display hex_digit_display_1 (.value(Length));  // open: dp
  Comparator #(.width(1)) comparator_5 (.a(Ccontrol_Letter), .b(There_is_match), .eq(comparator_5_eq));  // open: gt, lt
  Comparator #(.width(4)) comparator_6 (.a(counter_4_q), .b(4'b0000), .gt(There_is_match), .eq(No_Match));  // open: lt
  Comparator #(.width(7)) comparator_7 (.a({7{1'b0}}), .b(Letter_input), .eq(\İnput_0 ));  // open: gt, lt
  Counter #(.width(3), .max('h7), .ongoal("stay")) counter_5 (
    .count(Accept_full_word_display), .Q(counter_5_q), .clk(Clk), .clr(Reset1));  // open: load, D, carry
  Register #(.width(3)) register_2 (.D(counter_1_q), .en(comparator_5_eq), .Q(\LOCATİON ), .clk(Clk), .clr(RESET_2));
  Multiplexer #(.width(3)) multiplexer_3 (
    .in0(counter_5_q), .in1(\LOCATİON ), .out(Rom_A), .sel(Ccontrol_Letter));  // open: en
  and and_2 (and_2_out, Accept_full_word_display, comparator_9_lt);
  or or_1 (enable_tty, and_2_out, Ccontrol_Letter);
  Counter #(.max('h9), .ongoal("stay")) counter_6 (
    .count(Accept_full_word_display), .Q(counter_6_q), .clk(Clk), .clr(Reset1));  // open: load, D, carry
  Comparator #(.width(4), .mode("unsigned")) comparator_8 (
    .a(Length), .b(4'b0000), .gt(comparator_8_gt));  // open: eq, lt
  Counter #(.width(4), .max('hf)) u_Faund (.Q(Faund_table), .clk(FAUND), .clr(Reset1));  // open: load, D, count, carry
  Counter #(.width(4), .max('hf)) counter_7 (
    .Q(\MİSS_TABLE ), .clk(\MİSS ), .clr(Reset1));  // open: load, D, count, carry
  Comparator comparator_9 (.a(counter_6_q), .b(8'h8), .lt(comparator_9_lt));  // open: gt, eq
  and and_3 (faund_2, comparator_8_gt, comparator_10_eq);
  Comparator #(.width(4)) comparator_10 (.a(Faund_table), .b(Length), .eq(comparator_10_eq));  // open: gt, lt
  Comparator #(.width(4)) comparator_11 (.a(\MİSS_TABLE ), .b(4'b1010), .eq(\mİSS_2 ));  // open: gt, lt

  assign ACCEPT = Accept_full_word_display;
  assign tty_clear = Reset1;

  // Notes on the sheet:
  //   Numbers of characters
endmodule
