// Logisim project Main Circuit.circ as structural Verilog: 1 circuit, main circuit main
module main (
  output [2:0] State_Table,
  output [6:0] Binary__Represent
);

  wire A_out, B_out, C_out, clock_1_out, D_out, E_out, F_out, G_out, H_out, I_out, J_out, K_out, L_out,
       M_out, main_2_accept, main_2_caunt_letter, main_2_enable_tty, main_2_faund_2, \main_2_i̇nput_0 ,
       \main_2_i̇nput__i̇nput_kontrol , \main_2_mi̇ss_2 , main_2_there_is_match, main_2_tty_clear,
       main_3_out_5, main_3_out_6, main_3_out_7, main_3_out_8, main_3_out_9, main_3_out_10, main_3_out_11,
       main_3_out_12, main_3_out_13, main_3_out_14, main_3_out_15, main_3_out_16, main_3_out_17,
       main_3_out_18, main_4_afwd, main_4_controled_letter, main_4_faound, main_4_load_input, \main_4_mi̇ss ,
       main_4_reset1, main_4_reset2, main_6_out_3, main_6_out_4, main_6_out_5, main_6_out_6, main_6_out_7,
       main_6_out_8, main_6_out_9, main_6_out_10, main_6_out_11, main_6_out_12, N_out, O_out, P_out, Q_out,
       R_out, Restart_out, S_out, T_out, U_out, V_out, W_out, X_out, Y_out, Z_out;
  wire [2:0] \main_2_locati̇on , main_2_rom_a;
  wire [3:0] main_2_length;
  wire [4:0] controlled_buffer_1_out;
  wire [6:0] demultiplexer_1_out0, demultiplexer_1_out1, demultiplexer_2_out0, demultiplexer_2_out1,
       demultiplexer_2_out2, demultiplexer_2_out3, demultiplexer_2_out4, demultiplexer_2_out5,
       demultiplexer_2_out6, demultiplexer_2_out7, main_1_out_2, main_1_out_3, main_1_out_4, main_1_out_5,
       main_1_out_6, main_1_out_7, main_1_out_8, main_1_out_9, multiplexer_1_out;
  wire [7:0] main_5_out_3, main_5_out_4, main_5_out_5, main_5_out_6, main_5_out_7, main_5_out_8,
       main_5_out_9, main_5_out_10;

  Clock clock_1 (.out(clock_1_out));
  RANDOM_WORD_main main_1 (
    .in_1(Restart_out), .out_2(main_1_out_2), .out_3(main_1_out_3), .out_4(main_1_out_4),
    .out_5(main_1_out_5), .out_6(main_1_out_6), .out_7(main_1_out_7), .out_8(main_1_out_8),
    .out_9(main_1_out_9));
  assign controlled_buffer_1_out = A_out ? 5'b00001 : 5'bz;  // Controlled_Buffer controlled_buffer_1
  Button A (.out(A_out));
  assign controlled_buffer_1_out = B_out ? 5'b00010 : 5'bz;  // Controlled_Buffer controlled_buffer_2
  assign controlled_buffer_1_out = C_out ? 5'b00011 : 5'bz;  // Controlled_Buffer controlled_buffer_3
  assign controlled_buffer_1_out = D_out ? 5'b00100 : 5'bz;  // Controlled_Buffer controlled_buffer_4
  Final_data_path_main main_2 (
    .Accept_full_word_display(main_4_afwd), .in_2(main_1_out_2), .in_3(main_1_out_3), .in_4(main_1_out_4),
    .in_5(main_1_out_5), .in_6(main_1_out_6), .in_7(main_1_out_7), .in_8(main_1_out_8), .in_9(main_1_out_9),
    .Reset1(main_4_reset1), .Ccontrol_Letter(main_4_controled_letter), .Clk(clock_1_out),
    .RESET_2(main_4_reset2), .Letter_input(Binary__Represent), .FAUND(main_4_faound),
    .\Load_İnpput (main_4_load_input), .\MİSS (\main_4_mi̇ss ), .ACCEPT(main_2_accept), .Rom_A(main_2_rom_a),
    .\LOCATİON (\main_2_locati̇on ), .Length(main_2_length), .enable_tty(main_2_enable_tty),
    .There_is_match(main_2_there_is_match), .faund_2(main_2_faund_2), .tty_clear(main_2_tty_clear),
    .\İnput__İnput_Kontrol (\main_2_i̇nput__i̇nput_kontrol ), .\İnput_0 (\main_2_i̇nput_0 ),
    .\mİSS_2 (\main_2_mi̇ss_2 ), .CAUNT_LETTER(main_2_caunt_letter));  // open: Faund_table, No_Match, MİSS_TABLE
  Button E (.out(E_out));
  Button B (.out(B_out));
  Button C (.out(C_out));
  Button D (.out(D_out));
  assign controlled_buffer_1_out = E_out ? 5'b00101 : 5'bz;  // Controlled_Buffer controlled_buffer_5
  assign controlled_buffer_1_out = F_out ? 5'b00110 : 5'bz;  // Controlled_Buffer controlled_buffer_6
  assign controlled_buffer_1_out = G_out ? 5'b00111 : 5'bz;  // Controlled_Buffer controlled_buffer_7
  Multiplexer #(.select(3), .width(7)) multiplexer_1 (
    .in0(main_1_out_2), .in1(main_1_out_3), .in2(main_1_out_4), .in3(main_1_out_5), .in4(main_1_out_6),
    .in5(main_1_out_7), .in6(main_1_out_8), .in7(main_1_out_9), .out(multiplexer_1_out), .sel(main_2_rom_a));  // open: en
  Button Restart (.out(Restart_out));
  Button G (.out(G_out));
  Button H (.out(H_out));
  Button F (.out(F_out));
  Button I (.out(I_out));
  assign controlled_buffer_1_out = H_out ? 5'b01000 : 5'bz;  // Controlled_Buffer controlled_buffer_8
  assign controlled_buffer_1_out = I_out ? 5'b01001 : 5'bz;  // Controlled_Buffer controlled_buffer_9
  Demultiplexer #(.width(7), .enable("false")) demultiplexer_1 (
    .out0(demultiplexer_1_out0), .out1(demultiplexer_1_out1), .in(multiplexer_1_out), .sel(main_2_accept));
  Button L (.out(L_out));
  Button M (.out(M_out));
  Button J (.out(J_out));
  Button K (.out(K_out));
  assign controlled_buffer_1_out = J_out ? 5'b01010 : 5'bz;  // Controlled_Buffer controlled_buffer_10
  assign controlled_buffer_1_out = K_out ? 5'b01011 : 5'bz;  // Controlled_Buffer controlled_buffer_11
  assign controlled_buffer_1_out = L_out ? 5'b01100 : 5'bz;  // Controlled_Buffer controlled_buffer_12
  Demultiplexer #(.select(3), .width(7), .enable("false")) demultiplexer_2 (
    .out0(demultiplexer_2_out0), .out1(demultiplexer_2_out1), .out2(demultiplexer_2_out2),
    .out3(demultiplexer_2_out3), .out4(demultiplexer_2_out4), .out5(demultiplexer_2_out5),
    .out6(demultiplexer_2_out6), .out7(demultiplexer_2_out7), .in(demultiplexer_1_out0),
    .sel(\main_2_locati̇on ));
  _7_Segment_Display u_7_segment_display_1 (
    .g(main_3_out_8), .f(main_3_out_7), .a(main_3_out_6), .b(main_3_out_5), .e(main_3_out_9),
    .d(main_3_out_10), .c(main_3_out_11));  // open: dp
  Button N (.out(N_out));
  Button P (.out(P_out));
  Button O (.out(O_out));
  Button Q (.out(Q_out));
  assign controlled_buffer_1_out = M_out ? 5'b01101 : 5'bz;  // Controlled_Buffer controlled_buffer_13
  assign controlled_buffer_1_out = N_out ? 5'b01110 : 5'bz;  // Controlled_Buffer controlled_buffer_14
  assign controlled_buffer_1_out = O_out ? 5'b01111 : 5'bz;  // Controlled_Buffer controlled_buffer_15
  assign controlled_buffer_1_out = P_out ? 5'b10000 : 5'bz;  // Controlled_Buffer controlled_buffer_16
  TTY #(.rows(1), .cols(3)) tty_1 (
    .data(demultiplexer_2_out0), .clk(clock_1_out), .we(main_2_enable_tty), .clr(main_2_tty_clear));
  Button U (.out(U_out));
  Button T (.out(T_out));
  Button R (.out(R_out));
  Button S (.out(S_out));
  ROM #(.addrWidth(5), .dataWidth(7)) rom_1 (.addr(controlled_buffer_1_out), .data(Binary__Represent));  // open: sel
  assign controlled_buffer_1_out = Q_out ? 5'b10001 : 5'bz;  // Controlled_Buffer controlled_buffer_17
  assign controlled_buffer_1_out = R_out ? 5'b10010 : 5'bz;  // Controlled_Buffer controlled_buffer_18
  TTY #(.rows(1), .cols(3)) tty_2 (
    .data(demultiplexer_2_out2), .clk(clock_1_out), .we(main_2_enable_tty), .clr(main_2_tty_clear));
  TTY #(.rows(1), .cols(3)) tty_3 (
    .data(demultiplexer_2_out3), .clk(clock_1_out), .we(main_2_enable_tty), .clr(main_2_tty_clear));
  TTY #(.rows(1), .cols(3)) tty_4 (
    .data(demultiplexer_2_out1), .clk(clock_1_out), .we(main_2_enable_tty), .clr(main_2_tty_clear));
  fikrt_score_bord_main main_3 (
    .out_5(main_3_out_5), .out_6(main_3_out_6), .out_7(main_3_out_7), .out_8(main_3_out_8),
    .out_9(main_3_out_9), .out_10(main_3_out_10), .out_11(main_3_out_11), .user(main_2_faund_2),
    .machine(\main_2_mi̇ss_2 ), .out_12(main_3_out_12), .out_13(main_3_out_13), .out_14(main_3_out_14),
    .out_15(main_3_out_15), .out_16(main_3_out_16), .out_17(main_3_out_17), .out_18(main_3_out_18));  // open: in_3, in_4
  _7_Segment_Display u_7_segment_display_2 (
    .g(main_3_out_15), .f(main_3_out_14), .a(main_3_out_13), .b(main_3_out_12), .e(main_3_out_16),
    .d(main_3_out_17), .c(main_3_out_18));  // open: dp
  Button Y (.out(Y_out));
  Button V (.out(V_out));
  Button X (.out(X_out));
  Button W (.out(W_out));
  assign controlled_buffer_1_out = S_out ? 5'b10011 : 5'bz;  // Controlled_Buffer controlled_buffer_19
  assign controlled_buffer_1_out = T_out ? 5'b10100 : 5'bz;  // Controlled_Buffer controlled_buffer_20
  assign controlled_buffer_1_out = U_out ? 5'b10101 : 5'bz;  // Controlled_Buffer controlled_buffer_21
  TTY #(.rows(1), .cols(3)) tty_5 (
    .data(demultiplexer_2_out5), .clk(clock_1_out), .we(main_2_enable_tty), .clr(main_2_tty_clear));
  TTY #(.rows(1), .cols(3)) tty_6 (
    .data(demultiplexer_2_out6), .clk(clock_1_out), .we(main_2_enable_tty), .clr(main_2_tty_clear));
  TTY #(.rows(1), .cols(3)) tty_7 (
    .data(demultiplexer_2_out4), .clk(clock_1_out), .we(main_2_enable_tty), .clr(main_2_tty_clear));
  cotrol_final_main main_4 (
    .FL(main_2_faund_2), .TM(main_2_there_is_match), .M(\main_2_mi̇ss_2 ), .clck(clock_1_out),
    .rR(Restart_out), .i1(\main_2_i̇nput_0 ), .i2(\main_2_i̇nput__i̇nput_kontrol ), .LC(main_2_caunt_letter),
    .reset2(main_4_reset2), .state_count(State_Table), .reset1(main_4_reset1),
    .load_input(main_4_load_input), .controled_Letter(main_4_controled_letter), .AFWD(main_4_afwd),
    .FAOUND(main_4_faound), .\mİSS (\main_4_mi̇ss ));
  Button Z (.out(Z_out));
  assign controlled_buffer_1_out = V_out ? 5'b10110 : 5'bz;  // Controlled_Buffer controlled_buffer_22
  assign controlled_buffer_1_out = W_out ? 5'b10111 : 5'bz;  // Controlled_Buffer controlled_buffer_23
  assign controlled_buffer_1_out = X_out ? 5'b11000 : 5'bz;  // Controlled_Buffer controlled_buffer_24
  TTY #(.rows(1), .cols(3)) tty_8 (
    .data(demultiplexer_2_out7), .clk(clock_1_out), .we(main_2_enable_tty), .clr(main_2_tty_clear));
  TTY #(.rows(1), .cols(9)) tty_9 (
    .data(demultiplexer_1_out1), .clk(clock_1_out), .we(main_2_enable_tty), .clr(main_2_tty_clear));
  assign controlled_buffer_1_out = Y_out ? 5'b11001 : 5'bz;  // Controlled_Buffer controlled_buffer_25
  assign controlled_buffer_1_out = Z_out ? 5'b11010 : 5'bz;  // Controlled_Buffer controlled_buffer_26
  Hex_Digit_Display hex_digit_display_1 (.value(main_2_length));  // open: dp
  DotMatrix #(.inputtype("row"), .matrixcols(8), .matrixrows(8)) dotmatrix_1 (
    .row0(main_5_out_3), .row1(main_5_out_4), .row2(main_5_out_5), .row3(main_5_out_6), .row4(main_5_out_7),
    .row5(main_5_out_8), .row6(main_5_out_9), .row7(main_5_out_10));
  \çöööp_adam_main  main_5 (
    .clk(\main_4_mi̇ss ), .reset(main_4_reset1), .out_3(main_5_out_3), .out_4(main_5_out_4),
    .out_5(main_5_out_5), .out_6(main_5_out_6), .out_7(main_5_out_7), .out_8(main_5_out_8),
    .out_9(main_5_out_9), .out_10(main_5_out_10));
  LED led_1 (.in(main_6_out_3));
  LED led_2 (.in(main_6_out_4));
  LED led_3 (.in(main_6_out_5));
  leds_main main_6 (
    .in_1(\main_4_mi̇ss ), .in_2(main_4_reset1), .out_3(main_6_out_3), .out_4(main_6_out_4),
    .out_5(main_6_out_5), .out_6(main_6_out_6), .out_7(main_6_out_7), .out_8(main_6_out_8),
    .out_9(main_6_out_9), .out_10(main_6_out_10), .out_11(main_6_out_11), .out_12(main_6_out_12));
  LED led_4 (.in(main_6_out_6));
  LED led_5 (.in(main_6_out_7));
  LED led_6 (.in(main_6_out_8));
  LED led_7 (.in(main_6_out_9));
  LED led_8 (.in(main_6_out_10));
  LED led_9 (.in(main_6_out_11));
  LED led_10 (.in(main_6_out_12));

  // Notes on the sheet:
  //   Clock
  //   Letter Button--->>>>
  //   Machine 
  //   contents of rom_1 (hex, n*v repeats v):
  //   0 61 62 63 64 65 66 67 68 69 6a 6b 6c 6d 6e 6f 70 71 72 73 74 75 76 77 78 79 7a
  //   Word
  //   User
  //   Answer
  //   Number Of Characters In Word
  //   Hanging Man
endmodule
