// Logisim project RANDOM WORD.circ as structural Verilog: 1 circuit, main circuit main
module main (
  input  in_1,
  output [6:0] out_2,
  output [6:0] out_3,
  output [6:0] out_4,
  output [6:0] out_5,
  output [6:0] out_6,
  output [6:0] out_7,
  output [6:0] out_8,
  output [6:0] out_9
);

  wire [2:0] random_1_out;
  wire [31:7] rom_1_data, rom_2_data;

  Random #(.width(3)) random_1 (.clk(in_1), .out(random_1_out));  // open: next, clr
  ROM #(.addrWidth(3), .dataWidth(32)) rom_1 (
    .addr(random_1_out),
    .data({rom_1_data[31], out_5, rom_1_data[23], out_4, rom_1_data[15], out_3, rom_1_data[7], out_2}));  // open: sel
  ROM #(.addrWidth(3), .dataWidth(32)) rom_2 (
    .addr(random_1_out),
    .data({rom_2_data[31], out_9, rom_2_data[23], out_8, rom_2_data[15], out_7, rom_2_data[7], out_6}));  // open: sel

  // Notes on the sheet:
  //   contents of rom_1 (hex, n*v repeats v):
  //   6b727574 69676f6c 706d6f63 78656c61 6d726f66 746163 7a6e6562 61747369
  //   contents of rom_2 (hex, n*v repeats v):
  //   7965 63 72657475 0 616c75 0 6e69 6c75626e
endmodule
