// Logisim project cotrol final.circ as structural Verilog: 1 circuit, main circuit main
module main (
  input  FL,
  input  TM,
  input  M,
  input  LC,
  input  i2,
  input  i1,
  input  clck,
  input  rR,
  output reset2,
  output [2:0] state_count,
  output reset1,
  output load_input,
  output controled_Letter,
  output AFWD,
  output FAOUND,
  output \mİSS 
);

  wire and_4_out, and_5_out, and_6_out, and_7_out, and_8_out, and_9_out, and_10_out, and_11_out, and_12_out,
       and_13_out, and_14_out, and_16_out, and_17_out, and_18_out, and_19_out, and_20_out, and_21_out,
       not_1_out, not_2_out, not_3_out, not_4_out, not_5_out, not_6_out, not_7_out, not_8_out, not_9_out,
       not_10_out, or_1_out;
  wire [2:0] N0_out;

  not not_1 (not_1_out, i2);
  not not_2 (not_2_out, i1);
  not not_3 (not_3_out, FL);
  not not_4 (not_4_out, rR);
  not not_5 (not_5_out, TM);
  not not_6 (not_6_out, LC);
  not not_7 (not_7_out, M);
  Register #(.width(3)) register_1 (.D(N0_out), .Q(state_count), .clk(clck));  // open: en, clr
  not not_8 (not_8_out, state_count[0]);
  not not_9 (not_9_out, state_count[1]);
  not not_10 (not_10_out, state_count[2]);
  and and_1 (reset2, not_9_out, not_10_out);
  and and_2 (reset1, not_10_out, not_9_out, not_8_out);
  and and_3 (load_input, not_10_out, state_count[1], not_8_out);
  or or_1 (or_1_out, i1, i2);
  and and_4 (and_4_out, TM, not_8_out, not_10_out, state_count[1]);
  and and_5 (and_5_out, not_8_out, not_9_out);
  and and_6 (and_6_out, not_9_out, not_10_out, state_count[0], or_1_out);
  and and_7 (and_7_out, not_10_out, state_count[1], state_count[0]);
  and and_8 (and_8_out, state_count[2], not_9_out, state_count[0], not_7_out, not_3_out);
  and and_9 (and_9_out, not_10_out, not_9_out, state_count[0], not_2_out, not_1_out);
  and and_10 (and_10_out, not_10_out, state_count[1], not_8_out, not_6_out);
  and and_11 (and_11_out, not_10_out, state_count[1], not_8_out, TM, LC);
  and and_12 (and_12_out, state_count[2], not_9_out, state_count[0], FL);
  and and_13 (and_13_out, state_count[2], not_9_out, state_count[0], M, not_3_out);
  and and_14 (and_14_out, state_count[1], state_count[2], not_8_out, not_4_out);
  and and_15 (controled_Letter, not_10_out, state_count[1], state_count[0]);
  and and_16 (and_16_out, state_count[2], not_9_out, state_count[0], FL);
  and and_17 (and_17_out, state_count[2], not_9_out, state_count[0], M, not_3_out);
  and and_18 (and_18_out, state_count[2], state_count[1], not_8_out, not_4_out);
  and and_19 (and_19_out, not_10_out, state_count[1], state_count[0]);
  and and_20 (and_20_out, state_count[2], not_9_out, not_8_out);
  and and_21 (and_21_out, not_10_out, state_count[1], not_8_out, not_5_out, LC);
  and and_22 (AFWD, state_count[2], state_count[1], not_8_out);
  or N0 (N0_out[0], and_4_out, and_5_out, and_6_out, and_7_out, and_8_out);
  and and_23 (FAOUND, not_10_out, state_count[1], state_count[0]);
  or N1 (N0_out[1], and_9_out, and_10_out, and_11_out, and_12_out, and_13_out, and_14_out);
  and and_24 (\mİSS , not_8_out, state_count[2], not_9_out);
  or N2 (N0_out[2], and_16_out, and_17_out, and_18_out, and_19_out, and_20_out, and_21_out);
endmodule
