// Logisim project fikrt score bord.circ as structural Verilog: 1 circuit, main circuit main
module main (
  input  user,
  input  machine,
  input  in_3,
  input  in_4,
  output out_5,
  output out_6,
  output out_7,
  output out_8,
  output out_9,
  output out_10,
  output out_11,
  output out_12,
  output out_13,
  output out_14,
  output out_15,
  output out_16,
  output out_17,
  output out_18
);

  wire [2:0] counter_1_q, counter_2_q;

  Counter #(.width(3), .max('h7)) counter_1 (.Q(counter_1_q), .clk(user), .clr(in_3));  // open: load, D, count, carry
  ROM #(.addrWidth(3), .dataWidth(1)) rom_1 (.addr(counter_1_q), .data(out_12));  // open: sel
  ROM #(.addrWidth(3), .dataWidth(1)) rom_2 (.addr(counter_1_q), .data(out_13));  // open: sel
  ROM #(.addrWidth(3), .dataWidth(1)) rom_3 (.addr(counter_1_q), .data(out_14));  // open: sel
  ROM #(.addrWidth(3), .dataWidth(1)) rom_4 (.addr(counter_1_q), .data(out_15));  // open: sel
  ROM #(.addrWidth(3), .dataWidth(1)) rom_5 (.addr(counter_1_q), .data(out_16));  // open: sel
  ROM #(.addrWidth(3), .dataWidth(1)) rom_6 (.addr(counter_1_q), .data(out_17));  // open: sel
  ROM #(.addrWidth(3), .dataWidth(1)) rom_7 (.addr(counter_1_q), .data(out_18));  // open: sel
  ROM #(.addrWidth(3), .dataWidth(1)) rom_8 (.addr(counter_2_q), .data(out_5));  // open: sel
  ROM #(.addrWidth(3), .dataWidth(1)) rom_9 (.addr(counter_2_q), .data(out_6));  // open: sel
  ROM #(.addrWidth(3), .dataWidth(1)) rom_10 (.addr(counter_2_q), .data(out_7));  // open: sel
  ROM #(.addrWidth(3), .dataWidth(1)) rom_11 (.addr(counter_2_q), .data(out_8));  // open: sel
  ROM #(.addrWidth(3), .dataWidth(1)) rom_12 (.addr(counter_2_q), .data(out_9));  // open: sel
  ROM #(.addrWidth(3), .dataWidth(1)) rom_13 (.addr(counter_2_q), .data(out_10));  // open: sel
  ROM #(.addrWidth(3), .dataWidth(1)) rom_14 (.addr(counter_2_q), .data(out_11));  // open: sel
  Counter #(.width(3), .max('h7)) counter_2 (
    .Q(counter_2_q), .clk(machine), .clr(in_4));  // open: load, D, count, carry

  // Notes on the sheet:
  //   contents of rom_1 (hex, n*v repeats v):
  //   4*1
  //   contents of rom_2 (hex, n*v repeats v):
  //   1 0 1 1
  //   contents of rom_3 (hex, n*v repeats v):
  //   1
  //   contents of rom_4 (hex, n*v repeats v):
  //   0 0 1 1
  //   contents of rom_5 (hex, n*v repeats v):
  //   1 0 1
  //   contents of rom_6 (hex, n*v repeats v):
  //   1 0 1 1
  //   contents of rom_7 (hex, n*v repeats v):
  //   1 1 0 1
  //   contents of rom_8 (hex, n*v repeats v):
  //   4*1
  //   contents of rom_9 (hex, n*v repeats v):
  //   1 0 1 1
  //   contents of rom_10 (hex, n*v repeats v):
  //   1
  //   contents of rom_11 (hex, n*v repeats v):
  //   0 0 1 1
  //   contents of rom_12 (hex, n*v repeats v):
  //   1 0 1
  //   contents of rom_13 (hex, n*v repeats v):
  //   1 0 1 1
  //   contents of rom_14 (hex, n*v repeats v):
  //   1 1 0 1
endmodule
