// Logisim project leds.circ as structural Verilog: 1 circuit, main circuit main
module main (
  input  in_1,
  input  in_2,
  output out_3,
  output out_4,
  output out_5,
  output out_6,
  output out_7,
  output out_8,
  output out_9,
  output out_10,
  output out_11,
  output out_12
);

  wire not_1_out, not_2_out, not_3_out, not_4_out, S1_out, S2_2_out, S2_3_out, S2_4_out, S2_5_out, S2_6_out,
       S2_7_out, S2_8_out, S2_9_out, S2_out;
  wire [3:0] counter_1_q;

  Counter #(.width(4), .max('hf)) counter_1 (.Q(counter_1_q), .clk(in_1), .clr(in_2));  // open: load, D, count, carry
  not not_1 (not_1_out, counter_1_q[0]);
  not not_2 (not_2_out, counter_1_q[1]);
  not not_3 (not_3_out, counter_1_q[2]);
  not not_4 (not_4_out, counter_1_q[3]);
  and S1 (S1_out, not_4_out, not_3_out, not_2_out, counter_1_q[0]);
  and S2 (S2_out, not_4_out, counter_1_q[1], not_4_out, not_1_out);
  and S2_2 (S2_2_out, not_4_out, not_3_out, counter_1_q[1], counter_1_q[0]);
  and S2_3 (S2_3_out, counter_1_q[2], not_1_out, not_2_out, not_4_out);
  and S2_4 (S2_4_out, counter_1_q[2], counter_1_q[0], not_2_out, not_4_out);
  and S2_5 (S2_5_out, counter_1_q[2], counter_1_q[1], not_4_out, not_1_out);
  and S2_6 (S2_6_out, counter_1_q[1], counter_1_q[2], counter_1_q[0], not_4_out);
  and S2_7 (S2_7_out, counter_1_q[3], not_1_out, not_2_out, not_3_out);
  and S2_8 (S2_8_out, counter_1_q[3], not_3_out, not_2_out, counter_1_q[0]);
  and S2_9 (S2_9_out, counter_1_q[3], not_3_out, not_1_out, counter_1_q[1]);
  or or_1 (out_8, S2_9_out, S2_8_out, S2_5_out, S2_7_out, S2_6_out);
  or or_2 (out_9, S2_9_out, S2_6_out, S2_8_out, S2_7_out);
  or or_3 (out_3, S2_9_out, S2_6_out, S2_5_out, S1_out, S2_out, S2_3_out, S2_4_out, S2_2_out, S2_7_out, out_6);
  or or_4 (out_5, out_6, out_6, S2_3_out, S2_6_out, S2_2_out, S2_5_out, S2_7_out, S2_9_out);
  or or_5 (out_6, S2_7_out, S2_5_out, S2_6_out, S2_4_out, S2_8_out, S2_3_out, S2_9_out);
  or or_6 (out_7, S2_6_out, S2_8_out, S2_5_out, S2_4_out, S2_7_out, S2_9_out);
  or or_7 (out_10, S2_9_out, S2_8_out, S2_7_out);
  or or_8 (out_11, S2_8_out, S2_9_out);
  buf or_9 (out_12, S2_9_out);  // OR_Gate
  or or_10 (out_4, S2_9_out, S2_6_out, S2_out, S2_2_out, S2_3_out, S2_4_out, S2_5_out, S2_7_out, out_6);
endmodule
