// Logisim project çöööp adam.circ as structural Verilog: 1 circuit, main circuit main
module main (
  input  clk,
  input  reset,
  output [7:0] out_3,
  output [7:0] out_4,
  output [7:0] out_5,
  output [7:0] out_6,
  output [7:0] out_7,
  output [7:0] out_8,
  output [7:0] out_9,
  output [7:0] out_10
);

  wire [7:0] counter_1_q;

  Counter #(.max('ha), .ongoal("stay")) counter_1 (
    .Q(counter_1_q), .clk(clk), .clr(reset));  // open: load, D, count, carry
  ROM rom_1 (.addr(counter_1_q), .data(out_3));  // open: sel
  ROM rom_2 (.addr(counter_1_q), .data(out_4));  // open: sel
  ROM rom_3 (.addr(counter_1_q), .data(out_5));  // open: sel
  ROM rom_4 (.addr(counter_1_q), .data(out_6));  // open: sel
  ROM rom_5 (.addr(counter_1_q), .data(out_7));  // open: sel
  ROM rom_6 (.addr(counter_1_q), .data(out_8));  // open: sel
  ROM rom_7 (.addr(counter_1_q), .data(out_9));  // open: sel
  ROM rom_8 (.addr(counter_1_q), .data(out_10));  // open: sel

  // Notes on the sheet:
  //   contents of rom_1 (hex, n*v repeats v):
  //   4*0 20 7*3e
  //   contents of rom_2 (hex, n*v repeats v):
  //   4*0 20 20 38 4*3a
  //   contents of rom_3 (hex, n*v repeats v):
  //   4*0 20 20 30 32 32 32 37
  //   contents of rom_4 (hex, n*v repeats v):
  //   4*0 20 20 20 4*22
  //   contents of rom_5 (hex, n*v repeats v):
  //   4*0 20 20 20 4*22
  //   contents of rom_6 (hex, n*v repeats v):
  //   0 0 0 5*20 24 25 25 25
  //   contents of rom_7 (hex, n*v repeats v):
  //   0 0 9*70
  //   contents of rom_8 (hex, n*v repeats v):
  //   0 10*f8
endmodule
