// Logisim project 1801042693.circ as structural Verilog: 1 circuit, main circuit main
module main (
);

  wire and_1_out, and_2_out, and_3_out, and_5_out, and_6_out, and_7_out, and_9_out, and_10_out, and_11_out,
       and_12_out, and_13_out, and_14_out, and_15_out, and_16_out, and_17_out, and_18_out, and_19_out,
       and_20_out, and_21_out, and_22_out, and_23_out, and_24_out, and_25_out, button_1_out, button_2_out,
       button_3_out, clock_1_out, clock_2_out, clock_3_out, demultiplexer_1_out0, demultiplexer_1_out1,
       demultiplexer_1_out2, demultiplexer_1_out3, demultiplexer_1_out4, demultiplexer_1_out5,
       demultiplexer_1_out6, not_1_out, not_2_out, not_3_out, not_4_out, not_5_out, not_6_out, not_7_out,
       not_8_out, not_9_out, not_10_out, not_11_out, not_12_out, not_13_out, not_14_out, not_15_out,
       not_16_out;
  wire [1:0] and_4_out, and_8_out, register_1_q, register_2_q;
  wire [2:0] or_5_out, register_3_q;

  not not_1 (not_1_out, register_3_q[2]);
  not not_2 (not_2_out, register_3_q[1]);
  Register #(.width(2)) register_1 (.D(and_4_out), .en(1'b1), .Q(register_1_q), .clk(clock_1_out));  // open: clr
  not not_3 (not_3_out, register_3_q[0]);
  not not_4 (not_4_out, and_1_out);
  not not_5 (not_5_out, register_1_q[1]);
  not not_6 (not_6_out, register_1_q[1]);
  not not_7 (not_7_out, register_1_q[0]);
  not not_8 (not_8_out, register_1_q[1]);
  not not_9 (not_9_out, register_1_q[0]);
  Clock clock_1 (.out(clock_1_out));
  Register #(.width(2)) register_2 (.D(and_8_out), .en(1'b1), .Q(register_2_q), .clk(clock_2_out));  // open: clr
  Clock clock_2 (.out(clock_2_out));
  LED led_1 (.in(demultiplexer_1_out3));
  not not_10 (not_10_out, button_1_out);
  not not_11 (not_11_out, and_5_out);
  and and_1 (and_1_out, not_5_out, register_1_q[0]);
  and and_2 (and_2_out, button_3_out, not_6_out, register_1_q[0]);
  and and_3 (and_3_out, button_3_out, not_7_out, register_1_q[1]);
  and and_4 (and_4_out[0], button_3_out, not_8_out, not_9_out);
  not not_12 (not_12_out, register_2_q[1]);
  not not_13 (not_13_out, register_2_q[1]);
  not not_14 (not_14_out, register_2_q[0]);
  not not_15 (not_15_out, register_2_q[1]);
  not not_16 (not_16_out, register_2_q[0]);
  Button button_1 (.out(button_1_out));
  Button button_2 (.out(button_2_out));
  LED led_2 (.in(demultiplexer_1_out2));
  LED led_3 (.in(demultiplexer_1_out1));
  LED led_4 (.in(demultiplexer_1_out0));
  or or_1 (and_4_out[1], and_2_out, and_3_out);
  and and_5 (and_5_out, not_12_out, register_2_q[0]);
  and and_6 (and_6_out, button_2_out, not_13_out, register_2_q[0]);
  and and_7 (and_7_out, button_2_out, not_14_out, register_2_q[1]);
  and and_8 (and_8_out[0], button_2_out, not_15_out, not_16_out);
  Button button_3 (.out(button_3_out));
  LED led_5 (.in(demultiplexer_1_out5));
  LED led_6 (.in(demultiplexer_1_out6));
  LED led_7 (.in(demultiplexer_1_out4));
  and and_9 (and_9_out, register_3_q[2], not_2_out, not_11_out, not_10_out);
  and and_10 (and_10_out, register_3_q[2], not_2_out, and_1_out, not_10_out);
  and and_11 (and_11_out, register_3_q[2], not_2_out, register_3_q[0], not_10_out);
  and and_12 (and_12_out, register_3_q[2], register_3_q[1], not_3_out, not_10_out);
  and and_13 (and_13_out, not_2_out, not_3_out, and_1_out, not_11_out, not_10_out);
  and and_14 (and_14_out, not_1_out, register_3_q[1], not_4_out, not_10_out);
  and and_15 (and_15_out, not_1_out, register_3_q[1], and_5_out, not_10_out);
  and and_16 (and_16_out, not_1_out, register_3_q[1], register_3_q[0], not_10_out);
  and and_17 (and_17_out, register_3_q[2], register_3_q[1], not_3_out, not_10_out);
  and and_18 (and_18_out, not_1_out, register_3_q[0], not_4_out, and_5_out, not_10_out);
  and and_19 (and_19_out, register_3_q[2], not_2_out, register_3_q[0], and_1_out, not_11_out, not_10_out);
  and and_20 (and_20_out, not_1_out, register_3_q[1], register_3_q[0], not_10_out);
  and and_21 (and_21_out, not_1_out, not_3_out, not_4_out, and_5_out, not_10_out);
  and and_22 (and_22_out, not_2_out, register_3_q[0], not_4_out, not_11_out, not_10_out);
  and and_23 (and_23_out, not_2_out, register_3_q[0], and_1_out, and_5_out, not_10_out);
  and and_24 (and_24_out, not_1_out, register_3_q[1], and_1_out, not_11_out, not_10_out);
  and and_25 (and_25_out, register_3_q[2], not_2_out, not_3_out, and_1_out, not_11_out, not_10_out);
  or or_2 (and_8_out[1], and_6_out, and_7_out);
  Demultiplexer #(.select(3)) demultiplexer_1 (
    .out0(demultiplexer_1_out0), .out1(demultiplexer_1_out1), .out2(demultiplexer_1_out2),
    .out3(demultiplexer_1_out3), .out4(demultiplexer_1_out4), .out5(demultiplexer_1_out5),
    .out6(demultiplexer_1_out6), .in(1'b1), .sel(or_5_out));  // open: out7, en
  Register #(.width(3)) register_3 (.D(or_5_out), .en(1'b1), .Q(register_3_q), .clk(clock_3_out));  // open: clr
  Clock clock_3 (.out(clock_3_out));
  or or_3 (or_5_out[2], and_9_out, and_10_out, and_11_out, and_12_out, and_13_out);
  or or_4 (or_5_out[1], and_14_out, and_15_out, and_16_out, and_17_out, and_18_out, and_19_out);
  or or_5 (or_5_out[0], and_20_out, and_21_out, and_22_out, and_23_out, and_24_out, and_25_out);

  // Notes on the sheet:
  //   LEFT
  //   RESET
  //   RİGHT
endmodule
