// Logisim project Circuit.circ as structural Verilog: 1 circuit, main circuit main
module main (
  input  [15:0] NUMBER_OF_B,
  input  [15:0] NUMBER_OF_A,
  input  Start,
  output [2:0] STATE_COUNTER,
  output [15:0] RESULT
);

  wire clock_1_out, main_1_la, main_1_lb, main_1_lm, main_1_sa, main_1_sm, main_2_eq, main_2_gt, main_2_lt;

  controlunit_main main_1 (
    .gt(main_2_gt), .lt(main_2_lt), .eq(main_2_eq), .start(Start), .clk(clock_1_out),
    .stateout(STATE_COUNTER), .la(main_1_la), .sa(main_1_sa), .lb(main_1_lb), .sm(main_1_sm), .lm(main_1_lm));
  datapath_main main_2 (
    .sa(main_1_sa), .a_i(NUMBER_OF_A), .la(main_1_la), .clk(clock_1_out), .lb(main_1_lb), .b_i(NUMBER_OF_B),
    .sm(main_1_sm), .lm(main_1_lm), .gt(main_2_gt), .eq(main_2_eq), .lt(main_2_lt), .mult_result(RESULT));
  Clock clock_1 (.out(clock_1_out));
endmodule
