// Logisim project controlunit.circ as structural Verilog: 1 circuit, main circuit main
module main (
  input  gt,
  input  lt,
  input  eq,
  input  start,
  input  clk,
  output [2:0] stateout,
  output la,
  output sa,
  output lb,
  output sm,
  output lm
);

  wire and_1_out, and_2_out, and_3_out, and_4_out, and_5_out, and_6_out, and_7_out, not_1_out, not_2_out,
       not_3_out, or_2_out, or_3_out, s4_out;
  wire [2:0] and_9_out;

  Register #(.width(3)) state (.D(and_9_out), .en(1'b1), .Q(stateout), .clk(clk));  // open: clr
  not not_1 (not_1_out, stateout[0]);
  not not_2 (not_2_out, stateout[1]);
  not not_3 (not_3_out, stateout[2]);
  and and_1 (and_1_out, not_3_out, not_1_out, stateout[1], lt);
  and and_2 (and_2_out, not_3_out, not_1_out, stateout[1], eq);
  and and_3 (and_3_out, not_2_out, stateout[0]);
  and and_4 (and_4_out, not_1_out, stateout[1], gt);
  and and_5 (and_5_out, stateout[1], stateout[0]);
  and and_6 (and_6_out, not_2_out, start);
  and and_7 (and_7_out, stateout[1], gt);
  or or_1 (and_9_out[2], and_1_out, and_2_out);
  and and_8 (and_9_out[1], not_3_out, or_2_out);
  or or_2 (or_2_out, and_3_out, and_4_out, and_5_out);
  or or_3 (or_3_out, and_6_out, and_7_out);
  and and_9 (and_9_out[0], or_3_out, not_3_out, not_1_out);
  and s1 (lb, stateout[0], not_2_out, not_3_out);
  and s3 (sa, not_3_out, stateout[1], stateout[0]);
  and s4 (s4_out, stateout[2], not_1_out, not_2_out);
  or or_4 (la, lb, sa);
  or or_5 (lm, lb, sa, s4_out);

  assign sm = sa;
endmodule
