// Logisim project datapath.circ as structural Verilog: 1 circuit, main circuit main
module main (
  input  sa,
  input  [15:0] a_i,
  input  la,
  input  clk,
  input  lb,
  input  [15:0] b_i,
  input  sm,
  input  lm,
  output gt,
  output eq,
  output lt,
  output [15:0] mult_result
);

  wire [15:0] a_q, adder_1_out, b_q, multiplexer_1_out, multiplexer_2_out, subtractor_1_out;

  Multiplexer #(.width(16), .enable("false")) multiplexer_1 (
    .in0(a_i), .in1(subtractor_1_out), .out(multiplexer_1_out), .sel(sa));
  Register #(.width(16)) a (.D(multiplexer_1_out), .en(la), .Q(a_q), .clk(clk));  // open: clr
  Register #(.width(16)) b (.D(b_i), .en(lb), .Q(b_q), .clk(clk));  // open: clr
  Register #(.width(16)) mult (.D(multiplexer_2_out), .en(lm), .Q(mult_result), .clk(clk));  // open: clr
  Multiplexer #(.width(16), .enable("false")) multiplexer_2 (
    .in0({16{1'b0}}), .in1(adder_1_out), .out(multiplexer_2_out), .sel(sm));
  Subtractor #(.width(16)) subtractor_1 (.a(a_q), .b(16'h1), .out(subtractor_1_out), .bin(1'b0));  // open: bout
  Comparator #(.width(16)) comparator_1 (.a(a_q), .b({16{1'b0}}), .gt(gt), .eq(eq), .lt(lt));
  Adder #(.width(16)) adder_1 (.a(b_q), .b(mult_result), .out(adder_1_out), .cin(1'b0));  // open: cout

  // Notes on the sheet:
  //   ena
  //   enb
  //   clk
endmodule
